# Fritzing sketch Plan drone (saved by Fritzing 0.9.3b)
breadboards: 3

parts:
  Composant2 = NRF24L01+ Breakout Board
  Composant3 = Tri-Axis Gyro Breakout - L3G4200D
  Composant4 = Arduino Mega 2560 (Rev3)
  M1 = Keyes l9110 Fan module [package=THT]
  M2 = Keyes l9110 Fan module [package=THT]
  M3 = Keyes l9110 Fan module [package=THT]
  M4 = Keyes l9110 Fan module [package=THT]
  hc-sr1 = hc-sr04

nets:
  GND: Composant2.GND, Composant3.GND, Composant4.GND, M1.pin3, M2.pin3, M3.pin3, M4.pin3, hc-sr1.GND
  VCC: Composant2.VCC, Composant4.3V3
  N1: Composant2.CE, Composant4.D9_PWM
  N2: Composant2.CS, Composant4.D10_PWM
  N3: Composant2.SCK, Composant4.D52
  N4: Composant2.MOSI, Composant4.D51
  N5: Composant2.MISO, Composant4.D50
  VCC_2: Composant3.VCC, Composant4.5V, M1.pin4, M2.pin4, M3.pin4, M4.pin4, hc-sr1.VCC
  N6: Composant4.D2_PWM, M3.pin2
  N7: Composant4.D3_PWM, M4.pin2
  N8: Composant4.D4_PWM, M1.pin2
  N9: Composant4.D5_PWM, M2.pin1

notes:
  AV
  AR
  Gauche
  Droite

custom parts:
  Keyes l9110 Fan module: Keyes l9110 Fan module. Done from pictures without an actual board to hand so breadboard may not be fully accurate.
