# Fritzing sketch Radio Commande (saved by Fritzing 0.9.3b)

parts:
  Composant1 = Arduino Nano (Rev3.0)
  Composant2 = NRF24L01+ Breakout Board
  Composant3 = Thumb Joystick
  Composant4 = Thumb Joystick
  Composant6 = Standard LCD 16x2 white on blue [part_number=181]
  LCM1602_IIC1 = LCM1602 IIC [part_number="LCM1602 IIC" chip_label="LCM1602 IIC" package="DIP (Dual Inline) [THT]"]
  LED7 = Billie the Blue LED
  LED8 = Gus the Green LED
  S2 = Pushbutton [package="[SMD]"]
  S3 = Pushbutton [package="[SMD]"]
  R1 = Resistor [tolerance=±5% resistance=220 package="0805 [SMD]"]
  R2 = Resistor [tolerance=±5% resistance=220 package="0805 [SMD]"]

nets:
  N1: Composant1.D2, S3.Pin_4
  N2: Composant1.D3, S2.Pin_3, S2.Pin_4
  N3: Composant1.D4, LED8.anode
  N4: Composant1.D5, LED7.cathode
  N5: Composant1.D7, Composant3.SEL
  N6: Composant1.D8, Composant4.SEL
  N7: Composant1.D9, Composant2.CE
  N8: Composant1.D10, Composant2.CS
  N9: Composant1.D11/MOSI, Composant2.MOSI
  N10: Composant1.D12/MISO, Composant2.MISO
  GND: Composant1.GND, Composant2.GND, Composant3.GND, Composant4.GND, LCM1602_IIC1.GND, S2.Pin_1, S2.Pin_2, S3.Pin_2, R1.Pin_1, R2.Pin_1
  VCC: Composant1.5V, Composant3.VCC, Composant4.VCC, LCM1602_IIC1.VCC
  N11: Composant1.A5, LCM1602_IIC1.SCL
  N12: Composant1.A4, LCM1602_IIC1.SDA
  N13: Composant1.A3, Composant3.VERT
  N14: Composant1.A2, Composant3.HORZ
  N15: Composant1.A1, Composant4.VERT
  N16: Composant1.A0, Composant4.HORZ
  3V3: Composant1.3V3, Composant2.VCC
  N17: Composant1.D13/SCK, Composant2.SCK
  VSS: Composant6.VSS, LCM1602_IIC1.VSS
  VDD: Composant6.VDD, LCM1602_IIC1.VDD
  N18: Composant6.V0, LCM1602_IIC1.V0
  N19: Composant6.RS, LCM1602_IIC1.RS
  N20: Composant6.R/W, LCM1602_IIC1.RW
  N21: Composant6.E, LCM1602_IIC1.E
  N22: Composant6.DB0, LCM1602_IIC1.D0
  N23: Composant6.DB1, LCM1602_IIC1.D1
  N24: Composant6.DB2, LCM1602_IIC1.D2
  N25: Composant6.DB3, LCM1602_IIC1.D3
  N26: Composant6.DB4, LCM1602_IIC1.D4
  N27: Composant6.DB5, LCM1602_IIC1.D5
  N28: Composant6.DB6, LCM1602_IIC1.D6
  N29: Composant6.DB7, LCM1602_IIC1.D7
  N30: Composant6.LED+, LCM1602_IIC1.A
  N31: Composant6.LED-, LCM1602_IIC1.K
  N32: LCM1602_IIC1.LED_A, LCM1602_IIC1.LED_B
  N33: LED7.anode, R1.Pin_0
  N34: LED8.cathode, R2.Pin_0

notes:
  AV
  |
  GAUCHE -- +-- DROITE
  |
  AR
  SW1 = Fonction 1
  MONTEE
  |
  Rot G --+-- Rot D
  |
  DESCENTE
  SW2 = Fonction 2
  P1 (BP Drone On/Off)
  P2 (non utilisé)
  L1 (Retour Drone démarré)
  L2 (non utilisé)
  Emetteur NRF 2,4 GHz

custom parts:
  Standard LCD 16x2 white on blue: Standard HD44780 LCDs are useful for creating standalone projects. * 16 characters wide, 2 rows * White text on blue background * Connection port is 0.1" pitch, single row for easy breadboarding and wiring
  LCM1602 IIC: I2C-Module to use a 1602 or 2004 LCD on with the wire.h libory Serial LCD Modul
